# Fritzing sketch Sketch (saved by Fritzing 0.9.3b)
breadboards: 1

parts:
  Raspberry_Pi_1 = Raspberry Pi 3 [part_number=RPI-3-V1.2]  # not connected
  WeMos_D1_Mini_Relay_Shield_V1 = WeMos D1 Mini Relay Shield V2  # not connected
  WeMos_D1_Mini_Relay_Shield_V2 = WeMos D1 Mini Relay Shield V2
  WeMos_D1_Mini_Relay_Shield_V3 = WeMos D1 Mini Relay Shield V2
  WeMos_D1_Mini_Relay_Shield_V4 = WeMos D1 Mini Relay Shield V2 [part_number=Reilay1]  # not connected

nets:
  N1: WeMos_D1_Mini_Relay_Shield_V2.NC, WeMos_D1_Mini_Relay_Shield_V3.NO
  N2: WeMos_D1_Mini_Relay_Shield_V2.NO, WeMos_D1_Mini_Relay_Shield_V3.NC

notes:
  VCC
  IN4
  IN3
  IN2
  IN1
  GND
  Transformer 1
  Transformer 2
